# Fritzing sketch schema (saved by Fritzing 0.9.2b)
breadboards: 1

parts:
  Onderdeel1 = Arduino Uno (Rev3)
  U1 = ESP8266 WiFi Module [part_number=ESP8266]
  U2 = TMP36 [package=to-92-kit]
  R1 = Resistor [tolerance=±5% resistance=4.7k package="0402 [SMD]"]
  R2 = Resistor [tolerance=±5% resistance=10k package="1206 [SMD]"]

nets:
  N1: Onderdeel1.A0, U2.VOUT
  N2: Onderdeel1.D10_PWM/SS, U1.TXD
  N3: Onderdeel1.D11_PWM/MOSI, U1.RXD
  N4: Onderdeel1.D7, R1.Pin_1
  3V3: Onderdeel1.3V3, U1.VCC, R2.Pin_1
  5V: Onderdeel1.5V, U2.VCC
  GND: Onderdeel1.GND, U1.GND, U2.GND
  N5: U1.CH_PD, R1.Pin_0, R2.Pin_0

custom parts:
  ESP8266 WiFi Module: Generic WiFi Module based on the ESP8266 with onboard PCB antenna and UART communications
